// Digital circuit CORE.dig as structural Verilog
module CORE (
  input  clk,
  input  RST,
  input  CLR
);

  wire ALUD_CO, ALUDH_OE, ALUDL_OE, ALUS_OE, and_3_out, and_4_out, BR_Q, button_1_out, CLK_t,
       comparator_1_eq, comparator_1_gt, comparator_1_lt, DC_JUMP, IMMED_OE, IRQ_OE, not_1_out, not_2_out,
       RAM_OE, RAM_WE, RF_HWE, RF_LWE, RF_SFR, RFSRCR_WE, ROM_OE, SFR_OE, SR_WE, WR_WE, XRAM_OE;
  wire [2:0] BR_SRC, BUS_SRC, JUMP_TYPE;
  wire [3:0] ALUSD_FUNC, RF_SRC;
  wire [5:0] multiplexer_2_out;
  wire [6:0] and_2_out;
  wire [7:0] DBUS, IMMED, RF_Q, SR_q, WR_q;
  wire [7:4] RFSRCR_q;
  wire [11:0] ADDRESS, dcouter_1_q;
  wire [47:44] DECODER_2_d;

  Comparator #(.Bits(8)) comparator_1 (
    .a(RF_Q), .b(IMMED), .gt(comparator_1_gt), .eq(comparator_1_eq), .lt(comparator_1_lt));
  Decoder #(.Selector_Bits(3)) decoder_1 (
    .sel(BUS_SRC), .out_0(ALUS_OE), .out_1(ALUDL_OE), .out_2(ALUDH_OE), .out_3(IMMED_OE), .out_4(RAM_OE),
    .out_5(XRAM_OE), .out_6(ROM_OE), .out_7(IRQ_OE));
  DCOUTER #(.generic("Bits := 12;")) dcouter_1 (
    .CLK(CLK_t), .CLR(CLR), .CNT(1'b1), .LE(DC_JUMP), .D(ADDRESS), .Q(dcouter_1_q));
  Multiplexer #(.Selector_Bits(3)) multiplexer_1 (
    .sel(JUMP_TYPE), .in_0(1'b0), .in_1(1'b1), .in_2(comparator_1_gt), .in_3(comparator_1_eq),
    .in_4(comparator_1_lt), .in_5(BR_Q), .in_6(RST), .in_7(1'b0), .out(DC_JUMP));
  // Probe on dcouter_1_q
  ROM #(.AddrBits(12), .Bits(48)) DECODER_2 (
    .A(dcouter_1_q), .sel(1'b1),
    .D({DECODER_2_d, IMMED, ADDRESS, JUMP_TYPE, ALUSD_FUNC, RAM_WE, RFSRCR_WE, BR_SRC, SR_WE, WR_WE, BUS_SRC, RF_SFR, RF_HWE, RF_LWE, RF_SRC}));
  Register #(.Bits(8)) RFSRCR (.D(DBUS), .C(CLK_t), .en(RFSRCR_WE), .Q({RFSRCR_q, and_2_out[3:0]}));
  and and_1 (and_2_out[5], RFSRCR_q[4], RAM_WE);
  and and_2 (and_2_out[6], RFSRCR_q[4], RAM_OE);
  Multiplexer #(.Bits(7)) multiplexer_2 (
    .sel(RF_SFR), .in_0({1'b0, RF_HWE, RF_LWE, RF_SRC}),
    .in_1({and_2_out[6:5], and_2_out[5], and_2_out[3:0]}), .out({SFR_OE, multiplexer_2_out}));
  // Probe on RF_SRC
  // Probe on RF_LWE
  // Probe on RF_HWE
  // Probe on RF_SFR
  // Probe on BUS_SRC
  // Probe on WR_WE
  // Probe on SR_WE
  // Probe on BR_SRC
  // Probe on RFSRCR_WE
  // Probe on RAM_WE
  // Probe on ALUSD_FUNC
  // Probe on JUMP_TYPE
  // Probe on ADDRESS
  // Probe on IMMED
  Button button_1 (.out(button_1_out));
  reg_file RF (
    .CLK(CLK_t), .RS(multiplexer_2_out[3:0]), .D(DBUS), .LLE(multiplexer_2_out[4]),
    .HLE(multiplexer_2_out[5]), .Q(RF_Q));
  BR BR (.CLK(CLK_t), .CLR(CLR), .S(BR_SRC), .ALUDF(ALUD_CO), .ALUSF(ALUD_CO), .A0(RF_Q[0]), .A7(RF_Q[7]), .Q(BR_Q));
  // SwitchDT switchdt_1: pin names not known; wires that end beside it: clk, button_1_out, CLK_t
  // Probe on DBUS
  PullDown #(.Bits(8)) pulldown_1 (.out(DBUS));
  // Probe on RF_Q
  reg__sync_clear #(.generic("Bits := 8;")) WR (.D(DBUS), .CLK(CLK_t), .CLR(CLR), .nLE(WR_WE), .Q(WR_q));
  reg__sync_clear #(.generic("Bits := 8;")) SR (.D(DBUS), .CLK(CLK_t), .CLR(CLR), .nLE(SR_WE), .Q(SR_q));
  not not_1 (not_1_out, CLK_t);
  // Probe on WR_q
  // Probe on SR_q
  and and_3 (and_3_out, CLK_t, not_1_out);
  and and_4 (and_4_out, RAM_WE, and_3_out);
  // Probe on {SR_q, WR_q}
  not not_2 (not_2_out, SR_q[7]);
  ALU ALU (
    .A(RF_Q), .B(WR_q), .S(ALUSD_FUNC), .CI(BR_Q), .nSOE(ALUS_OE), .nDLOE(ALUDL_OE), .nDHOE(ALUDH_OE),
    .O(DBUS), .CO(ALUD_CO));
  ROM #(.AddrBits(16), .Bits(8)) ROM (.A({SR_q, WR_q}), .sel(ROM_OE), .D(DBUS));
  RAMSinglePortSel #(.AddrBits(7), .isProgramMemory("true"), .Bits(8)) RAM (
    .A(SR_q[6:0]), .CS(not_2_out), .WE(and_4_out), .OE(RAM_OE), .D(DBUS));
  assign DBUS = SFR_OE ? RF_Q : 8'bz;  // Driver driver_1
  assign DBUS = IMMED_OE ? IMMED : 8'bz;  // Driver driver_2

  // Notes on the sheet:
  //   clk: Hz: 2147483647
  //   contents of DECODER_2 (hex, n*v repeats v):
  //   b,c,d,10,13,14,16,17,1c,1e,20,22,24,27,28,29,2a,2d,2f,34,40,42,4e,5a,5c,5e,60,6c,
  //   78,7a,86,92,94,96,a2,ae,b0,bc,c8,ca,cc,ce,d0,dc,e8,ea,f6,102,104,106,112,11e,120,
  //   12c,138,13a,13c,13e,14a,156,158,164,170,172,174,180,18c,18e,19a,1a6,1a8,1aa,1ac,1ae,
  //   1b0,1bc,1c8,1ca,1d6,1e2,1e4,1e6,1f2,1fe,200,20c,218,21a,21c,21e,22a,236,238,244,250,
  //   252,254,260,26d,26f,272,273,274,27f,28c,28e,296,298,29e,2aa,2ac,2b8,2c4,2c6,2c8,2ca,
  //   2d6,2e2,2e4,2f0,2fc,2fe,300,30c,318,31a,326,332,334,336,338,33a,33c,33e,34a,356,358,
  //   364,370,372,374,381,384,385,386,388,389,38a,38b,38c,38e,38f,390,392,393,394,39a,39b,
  //   39c,39d,39e,39f,3a4,3a6,3b2,3be,3c0,3c2,3c4,3d0,3dc,3de,3ea,3f6,3f8,3fa,406,412,414,
  //   420,42c,42e,430,432,434,440,44c,44e,45a,466,468,46a,476,482,484,490,49c,49e,4a0,4a2,
  //   4ae,4ba,4bc,4c8,4d4,4d6,4d8,4e4,4f0,4f2,4fe,50a,50c,50e,510,512,514,520,52c,52e,53a,
  //   546,548,54a,556,562,564,570,57a,57c,57e,580,58c,598,59a,5a6,5b2,5b4,5b6,5c2,5ce,5d0,
  //   5dc,5e8,5ea,5ec,5ee,5f0,5fc,608,60a,616,622,624,626,632,63e,640,64c,658,65a,65c,65e,
  //   66a,676,678,684,690,692,694,6a0,6a8,6ad,6af,6b2,6bd,6c2,6d2,6d5,6d6,6d7,6da,6db,6e2,
  //   6e3,6e4,6e8,6e9,6eb,6ec,6f2,6f5,6f6,6f9,6fc,6fd,6fe,6ff,703,705,706,70d,70e,70f,710,
  //   711,712,713,714,715,716,717,718,719
  //   contents of ROM (hex, n*v repeats v):
  //   75,0,0,75,1,1,75,2,2,75,3,3,75,4,4,75,5,5,75,6,6,75,7,7,75,8,8,75,9,9,75,a,a,75,b,
  //   b,75,c,c,75,d,d,75,e,e,75,f,f,75,10,10,75,11,11,75,12,12,75,13,13,75,14,14,75,15,
  //   15,75,16,16,75,17,17,75,18,18,75,19,19,75,1a,1a,75,1b,1b,75,1c,1c,75,1d,1d,75,1e,
  //   1e,75,1f,1f,75,20,20,75,21,21,75,22,22,75,23,23,75,24,24,75,25,25,75,26,26,75,27,
  //   27,75,28,28,75,29,29,75,2a,2a,75,2b,2b,75,2c,2c,75,2d,2d,75,2e,2e,75,2f,2f,75,30,
  //   30,75,31,31,75,32,32,75,33,33,75,34,34,75,35,35,75,36,36,75,37,37,75,38,38,75,39,
  //   39,75,3a,3a,75,3b,3b,75,3c,3c,75,3d,3d,75,3e,3e,75,3f,3f,75,40,40,75,41,41,75,42,
  //   42,75,43,43,75,44,44,75,45,45,75,46,46,75,47,47,75,48,48,75,49,49,75,4a,4a,75,4b,
  //   4b,75,4c,4c,75,4d,4d,75,4e,4e,75,4f,4f,75,50,50,75,51,51,75,52,52,75,53,53,75,54,
  //   54,75,55,55,75,56,56,75,57,57,75,58,58,75,59,59,75,5a,5a,75,5b,5b,75,5c,5c,75,5d,
  //   5d,75,5e,5e,75,5f,5f,75,60,60,75,61,61,75,62,62,75,63,63,75,64,64,75,65,65,75,66,
  //   66,75,67,67,75,68,68,75,69,69,75,6a,6a,75,6b,6b,75,6c,6c,75,6d,6d,75,6e,6e,75,6f,
  //   6f,75,70,70,75,71,71,75,72,72,75,73,73,75,74,74,75,75,75,75,76,76,75,77,77,75,78,
  //   78,75,79,79,75,7a,7a,75,7b,7b,75,7c,7c,75,7d,7d,75,7e,7e,75,7f,7f,75,81,81,75,82,
  //   82,75,83,83,75,a8,a8,75,b8,b8,75,d0,d0,75,e0,e0,75,f0,f0
endmodule
